// Digital circuit 1bitALU.dig as structural Verilog
module _1bitALU (
  input  A,
  input  B,
  input  Ci,
  input  [1:0] op,
  output Co,
  output R
);

  wire and_1_out, or_1_out, stackingadder_1_r;

  and and_1 (and_1_out, A, B);
  or or_1 (or_1_out, A, B);
  Stackingadder stackingadder_1 (.A(A), .B(B), .Ci(Ci), .R(stackingadder_1_r), .CO(Co));
  Multiplexer #(.Selector_Bits(2)) multiplexer_1 (
    .sel(op), .in_0(and_1_out), .in_1(or_1_out), .in_2(stackingadder_1_r), .out(R));  // open: in_3
  // Pins of 1 and 2 bits meet at op
endmodule
