// Digital circuit 32adder.dig.dig as structural Verilog
module _32adder_dig (
  input  A23,
  input  B23,
  input  A22,
  input  B22,
  input  A21,
  input  B21,
  input  A20,
  input  B20,
  input  A19,
  input  B19,
  input  A18,
  input  B18,
  input  Ci,
  input  A17,
  input  B17,
  input  A16,
  input  B16,
  input  A15,
  input  B15,
  input  A14,
  input  B14,
  input  A13,
  input  B13,
  input  A12,
  input  B12,
  input  A11,
  input  B11,
  input  A10,
  input  B10,
  input  A9,
  input  B9,
  input  A8,
  input  B8,
  input  A7,
  input  B7,
  input  A6,
  input  B6,
  input  A5,
  input  B5,
  input  A4,
  input  B4,
  input  A3,
  input  B3,
  input  A2,
  input  B2,
  input  A1,
  input  B1,
  input  A0,
  input  B0,
  input  A29,
  input  B29,
  input  A28,
  input  B28,
  input  A27,
  input  B27,
  input  A26,
  input  B26,
  input  A25,
  input  B25,
  input  A24,
  input  B24,
  input  A31,
  input  B31,
  input  A30,
  input  B30,
  output S0,
  output Co,
  output S1,
  output S2,
  output S3,
  output S4,
  output S5,
  output S6,
  output S7,
  output S8,
  output S9,
  output S10,
  output S11,
  output S12,
  output S13,
  output S14,
  output S15,
  output S16,
  output S17,
  output S18,
  output S19,
  output S20,
  output S21,
  output S22,
  output S23,
  output S24,
  output S25,
  output S26,
  output S27,
  output S28,
  output S29,
  output S30,
  output S31
);

  wire stackingadder_2_co, stackingadder_3_co, stackingadder_4_co, stackingadder_5_co, stackingadder_6_co,
       stackingadder_7_co, stackingadder_8_co, stackingadder_9_co, stackingadder_10_co, stackingadder_11_co,
       stackingadder_12_co, stackingadder_13_co, stackingadder_14_co, stackingadder_15_co,
       stackingadder_16_co, stackingadder_17_co, stackingadder_18_co, stackingadder_19_co,
       stackingadder_20_co, stackingadder_21_co, stackingadder_22_co, stackingadder_23_co,
       stackingadder_24_co, stackingadder_25_co, stackingadder_26_co, stackingadder_27_co,
       stackingadder_28_co, stackingadder_29_co, stackingadder_30_co, stackingadder_31_co,
       stackingadder_32_co;

  Stackingadder stackingadder_1 (.A(A31), .B(B31), .Ci(stackingadder_2_co), .R(S31), .CO(Co));
  Stackingadder stackingadder_2 (.A(A30), .B(B30), .Ci(stackingadder_3_co), .R(S30), .CO(stackingadder_2_co));
  Stackingadder stackingadder_3 (.A(A29), .B(B29), .Ci(stackingadder_4_co), .R(S29), .CO(stackingadder_3_co));
  Stackingadder stackingadder_4 (.A(A28), .B(B28), .Ci(stackingadder_5_co), .R(S28), .CO(stackingadder_4_co));
  Stackingadder stackingadder_5 (.A(A27), .B(B27), .Ci(stackingadder_6_co), .R(S27), .CO(stackingadder_5_co));
  Stackingadder stackingadder_6 (.A(A26), .B(B26), .Ci(stackingadder_7_co), .R(S26), .CO(stackingadder_6_co));
  Stackingadder stackingadder_7 (.A(A25), .B(B25), .Ci(stackingadder_8_co), .R(S25), .CO(stackingadder_7_co));
  Stackingadder stackingadder_8 (.A(A24), .B(B24), .Ci(stackingadder_9_co), .R(S24), .CO(stackingadder_8_co));
  Stackingadder stackingadder_9 (.A(A23), .B(B23), .Ci(stackingadder_10_co), .R(S23), .CO(stackingadder_9_co));
  Stackingadder stackingadder_10 (.A(A22), .B(B22), .Ci(stackingadder_11_co), .R(S22), .CO(stackingadder_10_co));
  Stackingadder stackingadder_11 (.A(A21), .B(B21), .Ci(stackingadder_12_co), .R(S21), .CO(stackingadder_11_co));
  Stackingadder stackingadder_12 (.A(A20), .B(B20), .Ci(stackingadder_13_co), .R(S20), .CO(stackingadder_12_co));
  Stackingadder stackingadder_13 (.A(A19), .B(B19), .Ci(stackingadder_14_co), .R(S19), .CO(stackingadder_13_co));
  Stackingadder stackingadder_14 (.A(A18), .B(B18), .Ci(stackingadder_15_co), .R(S18), .CO(stackingadder_14_co));
  Stackingadder stackingadder_15 (.A(A17), .B(B17), .Ci(stackingadder_16_co), .R(S17), .CO(stackingadder_15_co));
  Stackingadder stackingadder_16 (.A(A16), .B(B16), .Ci(stackingadder_17_co), .R(S16), .CO(stackingadder_16_co));
  Stackingadder stackingadder_17 (.A(A15), .B(B15), .Ci(stackingadder_18_co), .R(S15), .CO(stackingadder_17_co));
  Stackingadder stackingadder_18 (.A(A14), .B(B14), .Ci(stackingadder_19_co), .R(S14), .CO(stackingadder_18_co));
  Stackingadder stackingadder_19 (.A(A13), .B(B13), .Ci(stackingadder_20_co), .R(S13), .CO(stackingadder_19_co));
  Stackingadder stackingadder_20 (.A(A12), .B(B12), .Ci(stackingadder_21_co), .R(S12), .CO(stackingadder_20_co));
  Stackingadder stackingadder_21 (.A(A11), .B(B11), .Ci(stackingadder_22_co), .R(S11), .CO(stackingadder_21_co));
  Stackingadder stackingadder_22 (.A(A10), .B(B10), .Ci(stackingadder_23_co), .R(S10), .CO(stackingadder_22_co));
  Stackingadder stackingadder_23 (.A(A9), .B(B9), .Ci(stackingadder_24_co), .R(S9), .CO(stackingadder_23_co));
  Stackingadder stackingadder_24 (.A(A8), .B(B8), .Ci(stackingadder_25_co), .R(S8), .CO(stackingadder_24_co));
  Stackingadder stackingadder_25 (.A(A7), .B(B7), .Ci(stackingadder_26_co), .R(S7), .CO(stackingadder_25_co));
  Stackingadder stackingadder_26 (.A(A6), .B(B6), .Ci(stackingadder_27_co), .R(S6), .CO(stackingadder_26_co));
  Stackingadder stackingadder_27 (.A(A5), .B(B5), .Ci(stackingadder_28_co), .R(S5), .CO(stackingadder_27_co));
  Stackingadder stackingadder_28 (.A(A4), .B(B4), .Ci(stackingadder_29_co), .R(S4), .CO(stackingadder_28_co));
  Stackingadder stackingadder_29 (.A(A3), .B(B3), .Ci(stackingadder_30_co), .R(S3), .CO(stackingadder_29_co));
  Stackingadder stackingadder_30 (.A(A2), .B(B2), .Ci(stackingadder_31_co), .R(S2), .CO(stackingadder_30_co));
  Stackingadder stackingadder_31 (.A(A1), .B(B1), .Ci(stackingadder_32_co), .R(S1), .CO(stackingadder_31_co));
  Stackingadder stackingadder_32 (.A(A0), .B(B0), .Ci(Ci), .R(S0), .CO(stackingadder_32_co));
endmodule
