// Digital circuit 12bitAdder.dig as structural Verilog
module _12bitAdder (
  input  A11,
  input  B11,
  input  A10,
  input  B10,
  input  A9,
  input  B9,
  input  A8,
  input  B8,
  input  A7,
  input  B7,
  input  A6,
  input  B6,
  input  A5,
  input  B5,
  input  A4,
  input  B4,
  input  A3,
  input  B3,
  input  A2,
  input  B2,
  input  A1,
  input  B1,
  input  A0,
  input  B0,
  output D11,
  output D10,
  output D9,
  output D8,
  output D7,
  output D6,
  output D5,
  output D4,
  output D3,
  output D2,
  output D1,
  output D0,
  output CO
);

  wire stackingadder_2_co, stackingadder_3_co, stackingadder_4_co, stackingadder_5_co, stackingadder_6_co,
       stackingadder_7_co, stackingadder_8_co, stackingadder_9_co, stackingadder_10_co, stackingadder_11_co,
       stackingadder_12_co;

  Stackingadder stackingadder_1 (.A(A11), .B(B11), .Ci(stackingadder_2_co), .R(D11), .CO(CO));
  Stackingadder stackingadder_2 (.A(A10), .B(B10), .Ci(stackingadder_3_co), .R(D10), .CO(stackingadder_2_co));
  Stackingadder stackingadder_3 (.A(A9), .B(B9), .Ci(stackingadder_4_co), .R(D9), .CO(stackingadder_3_co));
  Stackingadder stackingadder_4 (.A(A8), .B(B8), .Ci(stackingadder_5_co), .R(D8), .CO(stackingadder_4_co));
  Stackingadder stackingadder_5 (.A(A7), .B(B7), .Ci(stackingadder_6_co), .R(D7), .CO(stackingadder_5_co));
  Stackingadder stackingadder_6 (.A(A6), .B(B6), .Ci(stackingadder_7_co), .R(D6), .CO(stackingadder_6_co));
  Stackingadder stackingadder_7 (.A(A5), .B(B5), .Ci(stackingadder_8_co), .R(D5), .CO(stackingadder_7_co));
  Stackingadder stackingadder_8 (.A(A4), .B(B4), .Ci(stackingadder_9_co), .R(D4), .CO(stackingadder_8_co));
  Stackingadder stackingadder_9 (.A(A3), .B(B3), .Ci(stackingadder_10_co), .R(D3), .CO(stackingadder_9_co));
  Stackingadder stackingadder_10 (.A(A2), .B(B2), .Ci(stackingadder_11_co), .R(D2), .CO(stackingadder_10_co));
  Stackingadder stackingadder_11 (.A(A1), .B(B1), .Ci(stackingadder_12_co), .R(D1), .CO(stackingadder_11_co));
  Stackingadder stackingadder_12 (.A(A0), .B(B0), .Ci(1'b0), .R(D0), .CO(stackingadder_12_co));
endmodule
