// Digital circuit 12bitCounter.dig as structural Verilog
module _12bitCounter (
  input  C,
  output [11:0] Q,
  output Rollover
);

  wire [11:0] _12bitadder_1_d11, multiplexer_1_out;

  _12bitAdder _12bitadder_1 (
    .A11(Q[11]), .B11(1'b0), .A10(Q[10]), .B10(1'b0), .A9(Q[9]), .B9(1'b0), .A8(Q[8]), .B8(1'b0), .A7(Q[7]),
    .B7(1'b0), .A6(Q[6]), .B6(1'b0), .A5(Q[5]), .B5(1'b0), .A4(Q[4]), .B4(1'b0), .A3(Q[3]), .B3(1'b0),
    .A2(Q[2]), .B2(1'b1), .A1(Q[1]), .B1(1'b0), .A0(Q[0]), .B0(1'b0), .D11(_12bitadder_1_d11[11]),
    .D10(_12bitadder_1_d11[10]), .D9(_12bitadder_1_d11[9]), .D8(_12bitadder_1_d11[8]),
    .D7(_12bitadder_1_d11[7]), .D6(_12bitadder_1_d11[6]), .D5(_12bitadder_1_d11[5]),
    .D4(_12bitadder_1_d11[4]), .D3(_12bitadder_1_d11[3]), .D2(_12bitadder_1_d11[2]),
    .D1(_12bitadder_1_d11[1]), .D0(_12bitadder_1_d11[0]));  // open: CO
  Multiplexer #(.Bits(12)) multiplexer_1 (
    .sel(Rollover), .in_0(_12bitadder_1_d11), .in_1({12{1'b0}}), .out(multiplexer_1_out));
  Register #(.Bits(12)) register_1 (.D(multiplexer_1_out), .C(C), .en(1'b1), .Q(Q));
  and and_1 (Rollover, Q[11], Q[10], Q[9], Q[8], Q[7], Q[6], Q[5], Q[4], Q[3], Q[2]);
endmodule
