// Digital circuit 8bitAdder.dig as structural Verilog
module _8bitAdder (
  input  A7,
  input  B7,
  input  A6,
  input  B6,
  input  A5,
  input  B5,
  input  A4,
  input  B4,
  input  A3,
  input  B3,
  input  A2,
  input  B2,
  input  A1,
  input  B1,
  input  A0,
  input  B0,
  output D7,
  output D6,
  output D5,
  output D4,
  output D3,
  output D2,
  output D1,
  output D0,
  output Co
);

  wire stackingadder_2_co, stackingadder_3_co, stackingadder_4_co, stackingadder_5_co, stackingadder_6_co,
       stackingadder_7_co, stackingadder_8_co;

  Stackingadder stackingadder_1 (.A(A7), .B(B7), .Ci(stackingadder_2_co), .R(D7), .CO(Co));
  Stackingadder stackingadder_2 (.A(A6), .B(B6), .Ci(stackingadder_3_co), .R(D6), .CO(stackingadder_2_co));
  Stackingadder stackingadder_3 (.A(A5), .B(B5), .Ci(stackingadder_4_co), .R(D5), .CO(stackingadder_3_co));
  Stackingadder stackingadder_4 (.A(A4), .B(B4), .Ci(stackingadder_5_co), .R(D4), .CO(stackingadder_4_co));
  Stackingadder stackingadder_5 (.A(A3), .B(B3), .Ci(stackingadder_6_co), .R(D3), .CO(stackingadder_5_co));
  Stackingadder stackingadder_6 (.A(A2), .B(B2), .Ci(stackingadder_7_co), .R(D2), .CO(stackingadder_6_co));
  Stackingadder stackingadder_7 (.A(A1), .B(B1), .Ci(stackingadder_8_co), .R(D1), .CO(stackingadder_7_co));
  Stackingadder stackingadder_8 (.A(A0), .B(B0), .Ci(1'b1), .R(D0), .CO(stackingadder_8_co));

  // Notes on the sheet:
  //   Because both of the operations are subtracting, the carry in line will be set to one so that it will always add one as per the 2's compliment rule
endmodule
