// Digital circuit Stackingadder.dig as structural Verilog
module Stackingadder (
  input  A,
  input  B,
  input  Ci,
  output R,
  output CO
);

  wire and_1_out, and_2_out, and_3_out, xor_1_out;

  xor xor_1 (xor_1_out, Ci, A);
  and and_1 (and_1_out, A, Ci);
  and and_2 (and_2_out, A, B);
  and and_3 (and_3_out, B, Ci);
  or or_1 (CO, and_1_out, and_2_out, and_3_out);
  xor xor_2 (R, xor_1_out, B);
endmodule

/* Test case:
A B Ci CO R
0 0 0 0 0
0 0 1 0 1
0 1 0 0 1
0 1 1 1 0
1 0 0 0 1
1 0 1 1 0
1 1 0 1 0
1 1 1 1 1
*/
