// Digital circuit subtractor.dig as structural Verilog
module subtractor (
  input  S,
  input  [7:0] A,
  input  [7:0] B,
  output [7:0] Q
);

  wire [7:0] multiplexer_1_out, multiplexer_2_out, not_1_out, not_9_out;

  not not_1 (not_1_out[0], A[0]);
  not not_2 (not_1_out[1], A[1]);
  not not_3 (not_1_out[2], A[2]);
  not not_4 (not_1_out[3], A[3]);
  not not_5 (not_1_out[4], A[4]);
  not not_6 (not_1_out[5], A[5]);
  not not_7 (not_1_out[6], A[6]);
  not not_8 (not_1_out[7], A[7]);
  not not_9 (not_9_out[0], B[0]);
  not not_10 (not_9_out[1], B[1]);
  not not_11 (not_9_out[2], B[2]);
  not not_12 (not_9_out[3], B[3]);
  not not_13 (not_9_out[4], B[4]);
  not not_14 (not_9_out[5], B[5]);
  not not_15 (not_9_out[6], B[6]);
  not not_16 (not_9_out[7], B[7]);
  Multiplexer #(.Bits(8)) multiplexer_1 (.sel(S), .in_0(A), .in_1(not_1_out), .out(multiplexer_1_out));
  Multiplexer #(.Bits(8)) multiplexer_2 (.sel(S), .in_0(not_9_out), .in_1(B), .out(multiplexer_2_out));
  _8bitAdder _8bitadder_1 (
    .A7(multiplexer_1_out[7]), .B7(multiplexer_2_out[7]), .A6(multiplexer_1_out[6]),
    .B6(multiplexer_2_out[6]), .A5(multiplexer_1_out[5]), .B5(multiplexer_2_out[5]),
    .A4(multiplexer_1_out[4]), .B4(multiplexer_2_out[4]), .A3(multiplexer_1_out[3]),
    .B3(multiplexer_2_out[3]), .A2(multiplexer_1_out[2]), .B2(multiplexer_2_out[2]),
    .A1(multiplexer_1_out[1]), .B1(multiplexer_2_out[1]), .A0(multiplexer_1_out[0]),
    .B0(multiplexer_2_out[0]), .D7(Q[7]), .D6(Q[6]), .D5(Q[5]), .D4(Q[4]), .D3(Q[3]), .D2(Q[2]), .D1(Q[1]),
    .D0(Q[0]));  // open: Co

  // Notes on the sheet:
  //   S: 0= A-B
  //   1= B-A
endmodule
