// Digital circuit 8wayDMUX.dig as structural Verilog
module _8wayDMUX (
  input  I,
  input  [2:0] S,
  output O_0,
  output O_1,
  output O_2,
  output O_3,
  output O_4,
  output O_5,
  output O_6,
  output O_7
);

  wire dmux_1_o_0, dmux_1_o_1, dmux_2_o_0, dmux_2_o_1, dmux_3_o_0, dmux_3_o_1;

  DMUX dmux_1 (.I(I), .S(S[0]), .O_0(dmux_1_o_0), .O_1(dmux_1_o_1));
  DMUX dmux_2 (.I(dmux_1_o_0), .S(S[1]), .O_0(dmux_2_o_0), .O_1(dmux_2_o_1));
  DMUX dmux_3 (.I(dmux_1_o_1), .S(S[1]), .O_0(dmux_3_o_0), .O_1(dmux_3_o_1));
  DMUX dmux_4 (.I(dmux_2_o_0), .S(S[2]), .O_0(O_0), .O_1(O_1));
  DMUX dmux_5 (.I(dmux_2_o_1), .S(S[2]), .O_0(O_2), .O_1(O_3));
  DMUX dmux_6 (.I(dmux_3_o_0), .S(S[2]), .O_0(O_4), .O_1(O_5));
  DMUX dmux_7 (.I(dmux_3_o_1), .S(S[2]), .O_0(O_6), .O_1(O_7));
endmodule

/* Test case:
S I O_0 O_1 O_2 O_3 O_4 O_5 O_6 O_7
loop(i, 256)
	7 bits(1, i>>7) bits(8, i)
end loop
*/
