// Digital circuit 8wayMUX.dig as structural Verilog
module _8wayMUX (
  input  I_7,
  input  I_6,
  input  I_5,
  input  I_4,
  input  I_3,
  input  I_2,
  input  I_1,
  input  I_0,
  input  [2:0] S,
  output Out
);

  wire mux_1_o, mux_2_o, mux_3_o, mux_4_o, mux_5_o, mux_6_o;

  MUX mux_1 (.I_1(I_7), .I_0(I_6), .S(S[0]), .O(mux_1_o));
  MUX mux_2 (.I_1(I_5), .I_0(I_4), .S(S[0]), .O(mux_2_o));
  MUX mux_3 (.I_1(I_3), .I_0(I_2), .S(S[0]), .O(mux_3_o));
  MUX mux_4 (.I_1(I_1), .I_0(I_0), .S(S[0]), .O(mux_4_o));
  MUX mux_5 (.I_1(mux_1_o), .I_0(mux_2_o), .S(S[1]), .O(mux_5_o));
  MUX mux_6 (.I_1(mux_3_o), .I_0(mux_4_o), .S(S[1]), .O(mux_6_o));
  MUX mux_7 (.I_1(mux_5_o), .I_0(mux_6_o), .S(S[2]), .O(Out));
endmodule

/* Test case:
I_7 I_6 I_5 I_4 I_3 I_2 I_1 I_0 S Out
loop(i, 256)
	bits(8,i) 7 bits(1, i>>7)
end loop
*/
