// Digital circuit DMUX.dig as structural Verilog
module DMUX (
  input  I,
  input  S,
  output O_0,
  output O_1
);

  wire not_1_out;

  not not_1 (not_1_out, S);
  and and_1 (O_0, I, not_1_out);
  and and_2 (O_1, I, S);
endmodule
