// Digital circuit MUX.dig as structural Verilog
module MUX (
  input  I_1,
  input  I_0,
  input  S,
  output O
);

  wire and_1_out, and_2_out;

  and and_1 (and_1_out, I_1, S);
  and and_2 (and_2_out, I_0, ~S);  // And
  or or_1 (O, and_1_out, and_2_out);
endmodule
