// Digital circuit 32rcadderandsub.dig as structural Verilog
module _32rcadderandsub (
  input  A31,
  input  A30,
  input  A29,
  input  A28,
  input  A27,
  input  A26,
  input  A25,
  input  A24,
  input  A23,
  input  A22,
  input  A21,
  input  A20,
  input  A19,
  input  A18,
  input  A17,
  input  A16,
  input  A15,
  input  A14,
  input  A13,
  input  A12,
  input  A11,
  input  A10,
  input  A9,
  input  A8,
  input  A7,
  input  A6,
  input  A5,
  input  A4,
  input  A3,
  input  A2,
  input  A1,
  input  A0,
  input  Ci,
  input  B0,
  input  B1,
  input  B2,
  input  B3,
  input  B4,
  input  B5,
  input  B6,
  input  B7,
  input  B8,
  input  B9,
  input  B10,
  input  B11,
  input  B12,
  input  B13,
  input  B14,
  input  B15,
  input  B16,
  input  B17,
  input  B18,
  input  B19,
  input  B20,
  input  B21,
  input  B22,
  input  B23,
  input  B24,
  input  B25,
  input  B26,
  input  B27,
  input  B28,
  input  B29,
  input  B30,
  input  B31,
  output Co,
  output S31,
  output S30,
  output S29,
  output S28,
  output S27,
  output S26,
  output S25,
  output S24,
  output S23,
  output S22,
  output S21,
  output S20,
  output S19,
  output S18,
  output S17,
  output S16,
  output S15,
  output S14,
  output S13,
  output S12,
  output S11,
  output S10,
  output S9,
  output S8,
  output S7,
  output S6,
  output S5,
  output S4,
  output S3,
  output S2,
  output S1,
  output S0
);

  wire multiplexer_1_out, multiplexer_2_out, multiplexer_3_out, multiplexer_4_out, multiplexer_5_out,
       multiplexer_6_out, multiplexer_7_out, multiplexer_8_out, multiplexer_9_out, multiplexer_10_out,
       multiplexer_11_out, multiplexer_12_out, multiplexer_13_out, multiplexer_14_out, multiplexer_15_out,
       multiplexer_16_out, multiplexer_17_out, multiplexer_18_out, multiplexer_19_out, multiplexer_20_out,
       multiplexer_21_out, multiplexer_22_out, multiplexer_23_out, multiplexer_24_out, multiplexer_25_out,
       multiplexer_26_out, multiplexer_27_out, multiplexer_28_out, multiplexer_29_out, multiplexer_30_out,
       multiplexer_31_out, multiplexer_32_out, not_1_out, not_2_out, not_3_out, not_4_out, not_5_out,
       not_6_out, not_7_out, not_8_out, not_9_out, not_10_out, not_11_out, not_12_out, not_13_out,
       not_14_out, not_15_out, not_16_out, not_17_out, not_18_out, not_19_out, not_20_out, not_21_out,
       not_22_out, not_23_out, not_24_out, not_25_out, not_26_out, not_27_out, not_28_out, not_29_out,
       not_30_out, not_31_out, not_32_out, stackingadder_2_co, stackingadder_3_co, stackingadder_4_co,
       stackingadder_5_co, stackingadder_6_co, stackingadder_7_co, stackingadder_8_co, stackingadder_9_co,
       stackingadder_10_co, stackingadder_11_co, stackingadder_12_co, stackingadder_13_co,
       stackingadder_14_co, stackingadder_15_co, stackingadder_16_co, stackingadder_17_co,
       stackingadder_18_co, stackingadder_19_co, stackingadder_20_co, stackingadder_21_co,
       stackingadder_22_co, stackingadder_23_co, stackingadder_24_co, stackingadder_25_co,
       stackingadder_26_co, stackingadder_27_co, stackingadder_28_co, stackingadder_29_co,
       stackingadder_30_co, stackingadder_31_co, stackingadder_32_co;

  not not_1 (not_1_out, B3);
  not not_2 (not_2_out, B2);
  not not_3 (not_3_out, B1);
  not not_4 (not_4_out, B0);
  not not_5 (not_5_out, B31);
  not not_6 (not_6_out, B30);
  not not_7 (not_7_out, B29);
  not not_8 (not_8_out, B28);
  not not_9 (not_9_out, B27);
  not not_10 (not_10_out, B26);
  not not_11 (not_11_out, B25);
  not not_12 (not_12_out, B24);
  not not_13 (not_13_out, B23);
  not not_14 (not_14_out, B22);
  not not_15 (not_15_out, B21);
  not not_16 (not_16_out, B20);
  not not_17 (not_17_out, B19);
  not not_18 (not_18_out, B18);
  not not_19 (not_19_out, B17);
  not not_20 (not_20_out, B16);
  not not_21 (not_21_out, B15);
  not not_22 (not_22_out, B14);
  not not_23 (not_23_out, B13);
  not not_24 (not_24_out, B12);
  not not_25 (not_25_out, B11);
  not not_26 (not_26_out, B10);
  not not_27 (not_27_out, B9);
  not not_28 (not_28_out, B8);
  not not_29 (not_29_out, B7);
  not not_30 (not_30_out, B6);
  not not_31 (not_31_out, B5);
  not not_32 (not_32_out, B4);
  Multiplexer multiplexer_1 (.sel(Ci), .in_0(B2), .in_1(not_2_out), .out(multiplexer_1_out));
  Multiplexer multiplexer_2 (.sel(Ci), .in_0(B1), .in_1(not_3_out), .out(multiplexer_2_out));
  Multiplexer multiplexer_3 (.sel(Ci), .in_0(B0), .in_1(not_4_out), .out(multiplexer_3_out));
  Multiplexer multiplexer_4 (.sel(Ci), .in_0(B31), .in_1(not_5_out), .out(multiplexer_4_out));
  Multiplexer multiplexer_5 (.sel(Ci), .in_0(B30), .in_1(not_6_out), .out(multiplexer_5_out));
  Multiplexer multiplexer_6 (.sel(Ci), .in_0(B29), .in_1(not_7_out), .out(multiplexer_6_out));
  Multiplexer multiplexer_7 (.sel(Ci), .in_0(B28), .in_1(not_8_out), .out(multiplexer_7_out));
  Multiplexer multiplexer_8 (.sel(Ci), .in_0(B27), .in_1(not_9_out), .out(multiplexer_8_out));
  Multiplexer multiplexer_9 (.sel(Ci), .in_0(B26), .in_1(not_10_out), .out(multiplexer_9_out));
  Multiplexer multiplexer_10 (.sel(Ci), .in_0(B25), .in_1(not_11_out), .out(multiplexer_10_out));
  Multiplexer multiplexer_11 (.sel(Ci), .in_0(B24), .in_1(not_12_out), .out(multiplexer_11_out));
  Multiplexer multiplexer_12 (.sel(Ci), .in_0(B23), .in_1(not_13_out), .out(multiplexer_12_out));
  Multiplexer multiplexer_13 (.sel(Ci), .in_0(B22), .in_1(not_14_out), .out(multiplexer_13_out));
  Multiplexer multiplexer_14 (.sel(Ci), .in_0(B21), .in_1(not_15_out), .out(multiplexer_14_out));
  Multiplexer multiplexer_15 (.sel(Ci), .in_0(B20), .in_1(not_16_out), .out(multiplexer_15_out));
  Multiplexer multiplexer_16 (.sel(Ci), .in_0(B19), .in_1(not_17_out), .out(multiplexer_16_out));
  Multiplexer multiplexer_17 (.sel(Ci), .in_0(B18), .in_1(not_18_out), .out(multiplexer_17_out));
  Multiplexer multiplexer_18 (.sel(Ci), .in_0(B17), .in_1(not_19_out), .out(multiplexer_18_out));
  Multiplexer multiplexer_19 (.sel(Ci), .in_0(B16), .in_1(not_20_out), .out(multiplexer_19_out));
  Multiplexer multiplexer_20 (.sel(Ci), .in_0(B15), .in_1(not_21_out), .out(multiplexer_20_out));
  Multiplexer multiplexer_21 (.sel(Ci), .in_0(B14), .in_1(not_22_out), .out(multiplexer_21_out));
  Multiplexer multiplexer_22 (.sel(Ci), .in_0(B13), .in_1(not_23_out), .out(multiplexer_22_out));
  Multiplexer multiplexer_23 (.sel(Ci), .in_0(B12), .in_1(not_24_out), .out(multiplexer_23_out));
  Multiplexer multiplexer_24 (.sel(Ci), .in_0(B11), .in_1(not_25_out), .out(multiplexer_24_out));
  Multiplexer multiplexer_25 (.sel(Ci), .in_0(B10), .in_1(not_26_out), .out(multiplexer_25_out));
  Multiplexer multiplexer_26 (.sel(Ci), .in_0(B9), .in_1(not_27_out), .out(multiplexer_26_out));
  Multiplexer multiplexer_27 (.sel(Ci), .in_0(B8), .in_1(not_28_out), .out(multiplexer_27_out));
  Multiplexer multiplexer_28 (.sel(Ci), .in_0(B7), .in_1(not_29_out), .out(multiplexer_28_out));
  Multiplexer multiplexer_29 (.sel(Ci), .in_0(B6), .in_1(not_30_out), .out(multiplexer_29_out));
  Multiplexer multiplexer_30 (.sel(Ci), .in_0(B5), .in_1(not_31_out), .out(multiplexer_30_out));
  Multiplexer multiplexer_31 (.sel(Ci), .in_0(B4), .in_1(not_32_out), .out(multiplexer_31_out));
  Multiplexer multiplexer_32 (.sel(Ci), .in_0(B3), .in_1(not_1_out), .out(multiplexer_32_out));
  Stackingadder stackingadder_1 (.A(A31), .B(multiplexer_4_out), .Ci(stackingadder_2_co), .R(S31), .CO(Co));
  Stackingadder stackingadder_2 (
    .A(A30), .B(multiplexer_5_out), .Ci(stackingadder_3_co), .R(S30), .CO(stackingadder_2_co));
  Stackingadder stackingadder_3 (
    .A(A29), .B(multiplexer_6_out), .Ci(stackingadder_4_co), .R(S29), .CO(stackingadder_3_co));
  Stackingadder stackingadder_4 (
    .A(A28), .B(multiplexer_7_out), .Ci(stackingadder_5_co), .R(S28), .CO(stackingadder_4_co));
  Stackingadder stackingadder_5 (
    .A(A27), .B(multiplexer_8_out), .Ci(stackingadder_6_co), .R(S27), .CO(stackingadder_5_co));
  Stackingadder stackingadder_6 (
    .A(A26), .B(multiplexer_9_out), .Ci(stackingadder_7_co), .R(S26), .CO(stackingadder_6_co));
  Stackingadder stackingadder_7 (
    .A(A25), .B(multiplexer_10_out), .Ci(stackingadder_8_co), .R(S25), .CO(stackingadder_7_co));
  Stackingadder stackingadder_8 (
    .A(A24), .B(multiplexer_11_out), .Ci(stackingadder_9_co), .R(S24), .CO(stackingadder_8_co));
  Stackingadder stackingadder_9 (
    .A(A23), .B(multiplexer_12_out), .Ci(stackingadder_10_co), .R(S23), .CO(stackingadder_9_co));
  Stackingadder stackingadder_10 (
    .A(A22), .B(multiplexer_13_out), .Ci(stackingadder_11_co), .R(S22), .CO(stackingadder_10_co));
  Stackingadder stackingadder_11 (
    .A(A21), .B(multiplexer_14_out), .Ci(stackingadder_12_co), .R(S21), .CO(stackingadder_11_co));
  Stackingadder stackingadder_12 (
    .A(A20), .B(multiplexer_15_out), .Ci(stackingadder_13_co), .R(S20), .CO(stackingadder_12_co));
  Stackingadder stackingadder_13 (
    .A(A19), .B(multiplexer_16_out), .Ci(stackingadder_14_co), .R(S19), .CO(stackingadder_13_co));
  Stackingadder stackingadder_14 (
    .A(A18), .B(multiplexer_17_out), .Ci(stackingadder_15_co), .R(S18), .CO(stackingadder_14_co));
  Stackingadder stackingadder_15 (
    .A(A17), .B(multiplexer_18_out), .Ci(stackingadder_16_co), .R(S17), .CO(stackingadder_15_co));
  Stackingadder stackingadder_16 (
    .A(A16), .B(multiplexer_19_out), .Ci(stackingadder_17_co), .R(S16), .CO(stackingadder_16_co));
  Stackingadder stackingadder_17 (
    .A(A15), .B(multiplexer_20_out), .Ci(stackingadder_18_co), .R(S15), .CO(stackingadder_17_co));
  Stackingadder stackingadder_18 (
    .A(A14), .B(multiplexer_21_out), .Ci(stackingadder_19_co), .R(S14), .CO(stackingadder_18_co));
  Stackingadder stackingadder_19 (
    .A(A13), .B(multiplexer_22_out), .Ci(stackingadder_20_co), .R(S13), .CO(stackingadder_19_co));
  Stackingadder stackingadder_20 (
    .A(A12), .B(multiplexer_23_out), .Ci(stackingadder_21_co), .R(S12), .CO(stackingadder_20_co));
  Stackingadder stackingadder_21 (
    .A(A11), .B(multiplexer_24_out), .Ci(stackingadder_22_co), .R(S11), .CO(stackingadder_21_co));
  Stackingadder stackingadder_22 (
    .A(A10), .B(multiplexer_25_out), .Ci(stackingadder_23_co), .R(S10), .CO(stackingadder_22_co));
  Stackingadder stackingadder_23 (
    .A(A9), .B(multiplexer_26_out), .Ci(stackingadder_24_co), .R(S9), .CO(stackingadder_23_co));
  Stackingadder stackingadder_24 (
    .A(A8), .B(multiplexer_27_out), .Ci(stackingadder_25_co), .R(S8), .CO(stackingadder_24_co));
  Stackingadder stackingadder_25 (
    .A(A7), .B(multiplexer_28_out), .Ci(stackingadder_26_co), .R(S7), .CO(stackingadder_25_co));
  Stackingadder stackingadder_26 (
    .A(A6), .B(multiplexer_29_out), .Ci(stackingadder_27_co), .R(S6), .CO(stackingadder_26_co));
  Stackingadder stackingadder_27 (
    .A(A5), .B(multiplexer_30_out), .Ci(stackingadder_28_co), .R(S5), .CO(stackingadder_27_co));
  Stackingadder stackingadder_28 (
    .A(A4), .B(multiplexer_31_out), .Ci(stackingadder_29_co), .R(S4), .CO(stackingadder_28_co));
  Stackingadder stackingadder_29 (
    .A(A3), .B(multiplexer_32_out), .Ci(stackingadder_30_co), .R(S3), .CO(stackingadder_29_co));
  Stackingadder stackingadder_30 (
    .A(A2), .B(multiplexer_1_out), .Ci(stackingadder_31_co), .R(S2), .CO(stackingadder_30_co));
  Stackingadder stackingadder_31 (
    .A(A1), .B(multiplexer_2_out), .Ci(stackingadder_32_co), .R(S1), .CO(stackingadder_31_co));
  Stackingadder stackingadder_32 (.A(A0), .B(multiplexer_3_out), .Ci(Ci), .R(S0), .CO(stackingadder_32_co));
endmodule

/* Test case:
	Ci A31 A30 A29 A28 A27 A26 A25 A24 A23 A22 A21 A20 A19 A18 A17 A16 A15 A14 A13 A12 A11 A10 A9 A8 A7 A6 A5 A4 A3 A2 A1 A0 B31 B30 B29 B28 B27 B26 B25 B24 B23 B22 B21 B20 B19 B18 B17 B16 B15 B14 B13 B12 B11 B10 B9 B8 B7 B6 B5 B4 B3 B2 B1 B0 Co S31 S30 S29 S28 S27 S26 S25 S24 S23 S22 S21 S20 S19 S18 S17 S16 S15 S14 S13 S12 S11 S10 S9 S8 S7 S6 S5 S4 S3 S2 S1 S0
loop(A,256)
  loop(B,256)
	0 bits(32,A)    bits(32,B)   bits(33,A+B)
	1 bits(32,A)    bits(32,B)   bits(33,A+B+1)
  end loop
end loop
*/
