// Digital circuit ALU.dig as structural Verilog
module ALU (
  input  [31:0] A,
  input  [31:0] B,
  input  [1:0] op,
  output [31:0] C,
  output Overload,
  output Negative,
  output Zero
);

  wire _32rcadderandsub_1_co, or_1_out;
  wire [30:0] _32rcadderandsub_1_s0;

  or or_1 (or_1_out, op[0], op[1]);
  _32rcadderandsub _32rcadderandsub_1 (
    .A31(A[31]), .A30(A[30]), .A29(A[29]), .A28(A[28]), .A27(A[27]), .A26(A[26]), .A25(A[25]), .A24(A[24]),
    .A23(A[23]), .A22(A[22]), .A21(A[21]), .A20(A[20]), .A19(A[19]), .A18(A[18]), .A17(A[17]), .A16(A[16]),
    .A15(A[15]), .A14(A[14]), .A13(A[13]), .A12(A[12]), .A11(A[11]), .A10(A[10]), .A9(A[9]), .A8(A[8]),
    .A7(A[7]), .A6(A[6]), .A5(A[5]), .A4(A[4]), .A3(A[3]), .A2(A[2]), .A1(A[1]), .A0(A[0]), .Ci(or_1_out),
    .B0(B[0]), .B1(B[1]), .B2(B[2]), .B3(B[3]), .B4(B[4]), .B5(B[5]), .B6(B[6]), .B7(B[7]), .B8(B[8]),
    .B9(B[9]), .B10(B[10]), .B11(B[11]), .B12(B[12]), .B13(B[13]), .B14(B[14]), .B15(B[15]), .B16(B[16]),
    .B17(B[17]), .B18(B[18]), .B19(B[19]), .B20(B[20]), .B21(B[21]), .B22(B[22]), .B23(B[23]), .B24(B[24]),
    .B25(B[25]), .B26(B[26]), .B27(B[27]), .B28(B[28]), .B29(B[29]), .B30(B[30]), .B31(B[31]),
    .Co(_32rcadderandsub_1_co), .S31(Negative), .S30(_32rcadderandsub_1_s0[30]),
    .S29(_32rcadderandsub_1_s0[29]), .S28(_32rcadderandsub_1_s0[28]), .S27(_32rcadderandsub_1_s0[27]),
    .S26(_32rcadderandsub_1_s0[26]), .S25(_32rcadderandsub_1_s0[25]), .S24(_32rcadderandsub_1_s0[24]),
    .S23(_32rcadderandsub_1_s0[23]), .S22(_32rcadderandsub_1_s0[22]), .S21(_32rcadderandsub_1_s0[21]),
    .S20(_32rcadderandsub_1_s0[20]), .S19(_32rcadderandsub_1_s0[19]), .S18(_32rcadderandsub_1_s0[18]),
    .S17(_32rcadderandsub_1_s0[17]), .S16(_32rcadderandsub_1_s0[16]), .S15(_32rcadderandsub_1_s0[15]),
    .S14(_32rcadderandsub_1_s0[14]), .S13(_32rcadderandsub_1_s0[13]), .S12(_32rcadderandsub_1_s0[12]),
    .S11(_32rcadderandsub_1_s0[11]), .S10(_32rcadderandsub_1_s0[10]), .S9(_32rcadderandsub_1_s0[9]),
    .S8(_32rcadderandsub_1_s0[8]), .S7(_32rcadderandsub_1_s0[7]), .S6(_32rcadderandsub_1_s0[6]),
    .S5(_32rcadderandsub_1_s0[5]), .S4(_32rcadderandsub_1_s0[4]), .S3(_32rcadderandsub_1_s0[3]),
    .S2(_32rcadderandsub_1_s0[2]), .S1(_32rcadderandsub_1_s0[1]), .S0(_32rcadderandsub_1_s0[0]));
  nor nor_1 (Zero, _32rcadderandsub_1_s0[0], _32rcadderandsub_1_s0[1], _32rcadderandsub_1_s0[2], _32rcadderandsub_1_s0[3], _32rcadderandsub_1_s0[4], _32rcadderandsub_1_s0[5], _32rcadderandsub_1_s0[6], _32rcadderandsub_1_s0[7], _32rcadderandsub_1_s0[8], _32rcadderandsub_1_s0[9], _32rcadderandsub_1_s0[10], _32rcadderandsub_1_s0[11], _32rcadderandsub_1_s0[12], _32rcadderandsub_1_s0[13], _32rcadderandsub_1_s0[14], _32rcadderandsub_1_s0[15], _32rcadderandsub_1_s0[16], _32rcadderandsub_1_s0[17], _32rcadderandsub_1_s0[18], _32rcadderandsub_1_s0[19], _32rcadderandsub_1_s0[20], _32rcadderandsub_1_s0[21], _32rcadderandsub_1_s0[22], _32rcadderandsub_1_s0[23], _32rcadderandsub_1_s0[24], _32rcadderandsub_1_s0[25], _32rcadderandsub_1_s0[26], _32rcadderandsub_1_s0[27], _32rcadderandsub_1_s0[28], _32rcadderandsub_1_s0[29], _32rcadderandsub_1_s0[30], Negative);
  and and_1 (Overload, _32rcadderandsub_1_co, ~Negative, B[31], A[31]);  // And
  Multiplexer #(.Selector_Bits(2), .Bits(32)) multiplexer_1 (
    .sel(op), .in_0({Negative, _32rcadderandsub_1_s0}), .in_1({Negative, _32rcadderandsub_1_s0}),
    .in_2({{31{1'b0}}, Negative}), .in_3({{31{1'b0}}, Zero}), .out(C));
endmodule

/* Test case:
A B op C Overload Negative Zero
1 1 0 2 0 0 0
32 32 0 64 0 0 0
5 2 1 3 0 0 0
5 10 1 4294967291 0 1 0
2147483648 2147483648 0 0 1 0 1
1 4 2 1 0 1 0
4 1 2 0 0 0 0
11 11 3 1 0 0 1
12 11 3 0 0 0 0
*/
