// Digital circuit Program counter.dig as structural Verilog
module Program_counter (
  input  [31:0] D,
  input  reset,
  input  load,
  input  C,
  output [31:0] Q
);

  wire [31:0] add_1_s, multiplexer_1_out, multiplexer_2_out;

  Add #(.Bits(32)) add_1 (.a(Q), .b(32'h4), .c_i(1'b0), .s(add_1_s));  // open: c_o
  Multiplexer #(.Bits(32)) multiplexer_1 (.sel(load), .in_0(add_1_s), .in_1(D), .out(multiplexer_1_out));
  Multiplexer #(.Bits(32)) multiplexer_2 (
    .sel(reset), .in_0(multiplexer_1_out), .in_1({32{1'b0}}), .out(multiplexer_2_out));
  D_FF #(.Bits(32)) d_ff_1 (.D(multiplexer_2_out), .C(C), .Q(Q));  // open: nQ
endmodule

/* Test case:
D load reset C Q
123 0 0 C 4
loop (a,2)
20 0 1 C 0
1 1 0 0 0
1 1 0 C 1
1 0 0 C 5
end loop
12 0 0 C 9
3 0 1 C 0
3 0 0 C 4
3 1 0 C 3
3 0 0 C 7
*/
