// Digital circuit fulladder.dig as structural Verilog
module fulladder (
  input  C_i,
  input  A,
  input  B,
  output S,
  output C_O
);

  wire halfadder_1_c, halfadder_1_s, halfadder_2_c;

  halfadder halfadder_1 (.A(A), .B(B), .S(halfadder_1_s), .C(halfadder_1_c));
  halfadder halfadder_2 (.A(C_i), .B(halfadder_1_s), .S(S), .C(halfadder_2_c));
  or or_1 (C_O, halfadder_2_c, halfadder_1_c);
endmodule

/* Test case:
A B C_i C_O S
0 0  0   0  0
0 0  1   0  1
0 1  0   0  1
0 1  1   1  0
1 0  0   0  1
1 0  1   1  0
1 1  0   1  0
1 1  1   1  1
*/
