// Digital circuit halfadder.dig as structural Verilog
module halfadder (
  input  A,
  input  B,
  output S,
  output C
);

  xor xor_1 (S, A, B);
  and and_1 (C, A, B);

  // Notes on the sheet:
  //   C indicates whether both values are added. S indicates whether at least one was added
endmodule
