// Digital circuit rcadder.dig as structural Verilog
module rcadder (
  input  A3,
  input  B3,
  input  A2,
  input  B2,
  input  A1,
  input  B1,
  input  A0,
  input  B0,
  input  Ci,
  output Co,
  output S3,
  output S2,
  output S1,
  output S0
);

  wire fulladder_2_c_o, fulladder_3_c_o, fulladder_4_c_o;

  fulladder fulladder_1 (.C_i(fulladder_2_c_o), .A(A3), .B(B3), .S(S3), .C_O(Co));
  fulladder fulladder_2 (.C_i(fulladder_3_c_o), .A(A2), .B(B2), .S(S2), .C_O(fulladder_2_c_o));
  fulladder fulladder_3 (.C_i(fulladder_4_c_o), .A(A1), .B(B1), .S(S1), .C_O(fulladder_3_c_o));
  fulladder fulladder_4 (.C_i(Ci), .A(A0), .B(B0), .S(S0), .C_O(fulladder_4_c_o));

  // Notes on the sheet:
  //   This truth table would have 512 rows and 14 columns
endmodule

/* Test case:
	Ci A3 A2 A1 A0 B3 B2 B1 B0 Co S3 S2 S1 S0
loop(A,16)
  loop(B,16)
	0 bits(4,A)    bits(4,B)   bits(5,A+B)
	1 bits(4,A)    bits(4,B)   bits(5,A+B+1)
  end loop
end loop
*/
