// Digital circuit encoder.dig as structural Verilog
module encoder (
  input  i0,
  input  i1,
  input  i2,
  input  i3,
  input  i4,
  input  i5,
  input  i6,
  input  i7,
  input  i8,
  input  i9,
  input  iA,
  input  iB,
  input  iC,
  input  iD,
  input  iE,
  input  iF
);

  wire and_1_out;

  // Or or_1 has open pins: In_1=i1, In_2=i3, In_3=i5, In_4=i7, In_5=i9, In_6=iB, In_7=iD, In_8=iF, out=open
  // Or or_2 has open pins: In_1=i2, In_2=i3, In_3=i6, In_4=i7, In_5=iA, In_6=iB, In_7=iE, In_8=iF, out=open
  // Or or_3 has open pins: In_1=i4, In_2=i5, In_3=i6, In_4=i7, In_5=iC, In_6=iD, In_7=iE, In_8=iF, out=open
  // Or or_4 has open pins: In_1=i8, In_2=i9, In_3=iB, In_4=iD, In_5=iF, In_6=iA, In_7=iE, In_8=iC, out=open
  // And and_1 has open pins: In_1=open, In_2=open, out=and_1_out
  Multiplexer multiplexer_1 (.sel(and_1_out), .in_0(1'b0), .in_1(1'b1));  // open: out
  Multiplexer multiplexer_2 ();  // open: sel, in_0, in_1, out
  Multiplexer multiplexer_3 ();  // open: sel, in_0, in_1, out
  Multiplexer multiplexer_4 ();  // open: sel, in_0, in_1, out
endmodule
