// Digital circuit priorityencoder.dig as structural Verilog
module priorityencoder (
  input  i0,
  input  i1,
  input  i2,
  input  i3,
  input  i4,
  input  i5,
  input  i6,
  input  i7,
  input  i8,
  input  i9,
  input  iA,
  input  iB,
  input  iC,
  input  iD,
  input  iE,
  input  iF,
  output [3:0] out
);

  wire [3:0] multiplexer_1_out, multiplexer_2_out, multiplexer_3_out, multiplexer_4_out, multiplexer_5_out,
       multiplexer_6_out, multiplexer_7_out, multiplexer_8_out, multiplexer_9_out, multiplexer_10_out,
       multiplexer_11_out, multiplexer_12_out, multiplexer_13_out, multiplexer_14_out, multiplexer_15_out;

  Multiplexer #(.Bits(4)) multiplexer_1 (.sel(i0), .in_0(4'b0000), .in_1(4'b0000), .out(multiplexer_1_out));
  Multiplexer #(.Bits(4)) multiplexer_2 (.sel(i1), .in_0(multiplexer_1_out), .in_1(4'b0001), .out(multiplexer_2_out));
  Multiplexer #(.Bits(4)) multiplexer_3 (.sel(i2), .in_0(multiplexer_2_out), .in_1(4'b0010), .out(multiplexer_3_out));
  Multiplexer #(.Bits(4)) multiplexer_4 (.sel(i3), .in_0(multiplexer_3_out), .in_1(4'b0011), .out(multiplexer_4_out));
  Multiplexer #(.Bits(4)) multiplexer_5 (.sel(i4), .in_0(multiplexer_4_out), .in_1(4'b0100), .out(multiplexer_5_out));
  Multiplexer #(.Bits(4)) multiplexer_6 (.sel(i5), .in_0(multiplexer_5_out), .in_1(4'b0101), .out(multiplexer_6_out));
  Multiplexer #(.Bits(4)) multiplexer_7 (.sel(i6), .in_0(multiplexer_6_out), .in_1(4'b0110), .out(multiplexer_7_out));
  Multiplexer #(.Bits(4)) multiplexer_8 (.sel(i7), .in_0(multiplexer_7_out), .in_1(4'b0111), .out(multiplexer_8_out));
  Multiplexer #(.Bits(4)) multiplexer_9 (.sel(i8), .in_0(multiplexer_8_out), .in_1(4'b1000), .out(multiplexer_9_out));
  Multiplexer #(.Bits(4)) multiplexer_10 (.sel(i9), .in_0(multiplexer_9_out), .in_1(4'b1001), .out(multiplexer_10_out));
  Multiplexer #(.Bits(4)) multiplexer_11 (
    .sel(iA), .in_0(multiplexer_10_out), .in_1(4'b1010), .out(multiplexer_11_out));
  Multiplexer #(.Bits(4)) multiplexer_12 (
    .sel(iB), .in_0(multiplexer_11_out), .in_1(4'b1011), .out(multiplexer_12_out));
  Multiplexer #(.Bits(4)) multiplexer_13 (
    .sel(iC), .in_0(multiplexer_12_out), .in_1(4'b1100), .out(multiplexer_13_out));
  Multiplexer #(.Bits(4)) multiplexer_14 (
    .sel(iD), .in_0(multiplexer_13_out), .in_1(4'b1101), .out(multiplexer_14_out));
  Multiplexer #(.Bits(4)) multiplexer_15 (
    .sel(iE), .in_0(multiplexer_14_out), .in_1(4'b1110), .out(multiplexer_15_out));
  Multiplexer #(.Bits(4)) multiplexer_16 (.sel(iF), .in_0(multiplexer_15_out), .in_1(4'b1111), .out(out));
endmodule

/* Test case:
i0 i1 i2 i3 i4 i5 i6 i7 i8 i9 iA iB iC iD iE iF out
0 0 0 0 0 0 0 0 0 0 0 0 0 0 0 0 0
1 0 0 0 0 0 0 0 0 0 0 0 0 0 0 0 0
0 1 0 0 0 0 0 0 0 0 0 0 0 0 0 0 1
0 0 1 0 0 0 0 0 0 0 0 0 0 0 0 0 2
0 0 0 1 0 0 0 0 0 0 0 0 0 0 0 0 3
0 0 0 0 1 0 0 0 0 0 0 0 0 0 0 0 4
0 0 0 0 0 1 0 0 0 0 0 0 0 0 0 0 5
0 0 0 0 0 0 1 0 0 0 0 0 0 0 0 0 6
0 0 0 0 0 0 0 1 0 0 0 0 0 0 0 0 7
0 0 0 0 0 0 0 0 1 0 0 0 0 0 0 0 8
0 0 0 0 0 0 0 0 0 1 0 0 0 0 0 0 9
0 0 0 0 0 0 0 0 0 0 1 0 0 0 0 0 10
0 0 0 0 0 0 0 0 0 0 0 1 0 0 0 0 11
0 0 0 0 0 0 0 0 0 0 0 0 1 0 0 0 12
0 0 0 0 0 0 0 0 0 0 0 0 0 1 0 0 13
0 0 0 0 0 0 0 0 0 0 0 0 0 0 1 0 14
0 0 0 0 0 0 0 0 0 0 0 0 0 0 0 1 15
1 0 0 0 0 0 0 0 0 0 1 0 0 0 0 0 10
0 1 0 0 0 0 0 0 0 0 1 0 0 0 0 0 10
0 0 1 0 0 0 0 0 0 0 1 0 0 0 0 0 10
0 0 0 1 0 0 0 0 0 0 1 0 0 0 0 0 10
0 0 0 0 1 0 0 0 0 0 1 0 0 0 0 0 10
0 0 0 0 0 1 0 0 0 0 1 0 0 0 0 0 10
0 0 0 0 0 0 1 0 0 0 1 0 0 0 0 0 10
0 0 0 0 0 0 0 1 0 0 1 0 0 0 0 0 10
0 0 0 0 0 0 0 0 1 0 1 0 0 0 0 0 10
0 0 0 0 0 0 0 0 0 1 1 0 0 0 0 0 10
0 0 0 0 0 0 0 0 0 0 1 1 0 0 0 0 11
0 0 0 0 0 0 0 0 0 0 1 0 1 0 0 0 12
0 0 0 0 0 0 0 0 0 0 1 0 0 1 0 0 13
0 0 0 0 0 0 0 0 0 0 1 0 0 0 1 0 14
0 0 0 0 0 0 0 0 0 0 1 0 0 0 0 1 15
*/
