// Digital circuit sevenhex.dig as structural Verilog
module sevenhex (
);

  wire _0_out, _1_out, _2_out, _3_out, _4_out, _5_out, _6_out, _7_out, _8_out, _9_out, _10_out, _11_out,
       _12_out, _13_out, _14_out, _15_out;
  wire [3:0] priorityencoder_1_out;

  Button _0 (.out(_0_out));
  Button _1 (.out(_1_out));
  Button _2 (.out(_2_out));
  Button _3 (.out(_3_out));
  Button _4 (.out(_4_out));
  Button _5 (.out(_5_out));
  Button _6 (.out(_6_out));
  Button _7 (.out(_7_out));
  Button _8 (.out(_8_out));
  Button _9 (.out(_9_out));
  Button _10 (.out(_10_out));
  Button _11 (.out(_11_out));
  Button _12 (.out(_12_out));
  Button _13 (.out(_13_out));
  Button _14 (.out(_14_out));
  Button _15 (.out(_15_out));
  priorityencoder priorityencoder_1 (
    .i0(_0_out), .i1(_1_out), .i2(_2_out), .i3(_3_out), .i4(_4_out), .i5(_5_out), .i6(_6_out), .i7(_7_out),
    .i8(_8_out), .i9(_9_out), .iA(_10_out), .iB(_11_out), .iC(_12_out), .iD(_13_out), .iE(_14_out),
    .iF(_15_out), .out(priorityencoder_1_out));
  Seven_Seg_Hex seven_seg_hex_1 (.d(priorityencoder_1_out), .dp(1'b0));
endmodule
