// Digital circuit bit.dig as structural Verilog
module \bit  (
  input  C,
  input  WEnable,
  input  D,
  output Q
);

  wire d_ff_1_q;

  D_FF d_ff_1 (.D(WEnable), .C(C), .Q(d_ff_1_q));  // open: nQ
  D_FF d_ff_2 (.D(D), .C(d_ff_1_q), .Q(Q));  // open: nQ
endmodule

/* Test case:
C D WEnable Q 
0 0 0 0
1 0 0 0 
0 0 0 0 
1 1 0 0
1 1 1 0
1 1 0 0
C 0 0 0
C 1 0 0
C 1 1 1 
C 0 0 1 
C 0 1 0 
C 1 0 0
*/
