// Digital circuit byte.dig as structural Verilog
module \byte  (
  input  [7:0] D,
  input  C,
  input  WEnable,
  output [7:0] Q
);

  \bit  bit_1 (.C(C), .WEnable(WEnable), .D(D[0]), .Q(Q[0]));
  \bit  bit_2 (.C(C), .WEnable(WEnable), .D(D[1]), .Q(Q[1]));
  \bit  bit_3 (.C(C), .WEnable(WEnable), .D(D[2]), .Q(Q[2]));
  \bit  bit_4 (.C(C), .WEnable(WEnable), .D(D[3]), .Q(Q[3]));
  \bit  bit_5 (.C(C), .WEnable(WEnable), .D(D[4]), .Q(Q[4]));
  \bit  bit_6 (.C(C), .WEnable(WEnable), .D(D[5]), .Q(Q[5]));
  \bit  bit_7 (.C(C), .WEnable(WEnable), .D(D[6]), .Q(Q[6]));
  \bit  bit_8 (.C(C), .WEnable(WEnable), .D(D[7]), .Q(Q[7]));
endmodule

/* Test case:
	C D WEnable Q
loop (a, 8)
C (a) 0 0
end loop
loop (a, 8)
C (a) 1 (a)
end loop
C 0 0 7
C 0 1 0
*/
